# Fritzing sketch ArduinoProgrammer (saved by Fritzing 0.7.0b)
breadboards: 1

parts:
  Arduino1 = Arduino
  IC1 = IC, DIP package, 8 pins [chip_label=ATtiny spacing=300mil]
  C1 = Electrolytic Capacitor [capacitance=1µF package="100 mil [THT, electrolytic]"]
  R1 = Resistor [tolerance=±5% resistance=220 package=THT]
  LED1 = LED - 5mm [color="Red (633nm)" package="5 mm [THT]"]

nets:
  N1: Arduino1.GND, IC1.pin4, C1.-, LED1.cathode
  N2: Arduino1.D13, IC1.pin7
  N3: Arduino1.D12, IC1.pin6
  N4: Arduino1.D11, IC1.pin5
  N5: Arduino1.D10, IC1.pin1
  N6: Arduino1.RST, C1.+
  N7: Arduino1.+5V, IC1.pin8
  N8: IC1.pin2, R1.Pin_0
  N9: R1.Pin_1, LED1.anode
