# Fritzing sketch SN74HC595 (saved by Fritzing 0.7.10b)
breadboards: 1

parts:
  74HC5951 = 74HC595 [package="DIP16 [THT]"]
  C2 = Ceramic Capacitor [capacitance=100nF rated_voltage=35V package="200 mil [THT, multilayer]"]
  Arduino1 = Arduino
  LED13 = LED - 5mm [color="Red (633nm)" package="5 mm [THT]"]
  LED14 = LED - 5mm [color="Red (633nm)" package="5 mm [THT]"]
  LED15 = LED - 5mm [color="Red (633nm)" package="5 mm [THT]"]
  LED16 = LED - 5mm [color="Red (633nm)" package="5 mm [THT]"]
  LED17 = LED - 5mm [color="Red (633nm)" package="5 mm [THT]"]
  LED18 = LED - 5mm [color="Red (633nm)" package="5 mm [THT]"]
  LED19 = LED - 5mm [color="Red (633nm)" package="5 mm [THT]"]
  LED20 = LED - 5mm [color="Red (633nm)" package="5 mm [THT]"]
  R10 = Resistor [resistance=220 tolerance=±5% package=THT]
  R11 = Resistor [resistance=220 tolerance=±5% package=THT]
  R12 = Resistor [resistance=220 tolerance=±5% package=THT]
  R13 = Resistor [resistance=220 tolerance=±5% package=THT]
  R14 = Resistor [resistance=220 tolerance=±5% package=THT]
  R15 = Resistor [resistance=220 tolerance=±5% package=THT]
  R16 = Resistor [resistance=220 tolerance=±5% package=THT]
  R17 = Resistor [resistance=220 tolerance=±5% package=THT]

nets:
  N1: 74HC5951.Q1, R16.Pin_0
  N2: 74HC5951.Q2, R15.Pin_0
  N3: 74HC5951.Q3, R14.Pin_0
  N4: 74HC5951.Q4, R13.Pin_0
  N5: 74HC5951.Q5, R12.Pin_0
  N6: 74HC5951.Q6, R11.Pin_0
  N7: 74HC5951.Q7, R10.Pin_0
  GND: 74HC5951.GND, C2.0, Arduino1.GND, LED13.cathode, LED14.cathode, LED15.cathode, LED16.cathode, LED17.cathode, LED18.cathode, LED19.cathode, LED20.cathode
  5V: 74HC5951.MR, 74HC5951.VCC, Arduino1.+5V
  N8: 74HC5951.SH_CP, Arduino1.D12
  N9: 74HC5951.ST_CP, C2.1, Arduino1.D8
  N10: 74HC5951.DS, Arduino1.D11
  N11: 74HC5951.Q0, R17.Pin_0
  N12: LED13.anode, R14.Pin_1
  N13: LED14.anode, R17.Pin_1
  N14: LED15.anode, R16.Pin_1
  N15: LED16.anode, R15.Pin_1
  N16: LED17.anode, R11.Pin_1
  N17: LED18.anode, R10.Pin_1
  N18: LED19.anode, R12.Pin_1
  N19: LED20.anode, R13.Pin_1

notes:
  In this project, a 74HC595 shift register is used to control 8 LEDs with just 3 Arduino pins.
  Related example: http://www.arduino.cc/en/Tutorial/ShiftOut

// code stored in the sketch: Shift_Register.ino
/*
  Shift Register Example
 for 74HC595 shift register

 This sketch turns reads serial input and uses it to set the pins
 of a 74HC595 shift register.

 Hardware:
 * 74HC595 shift register attached to pins 2, 3, and 4 of the Arduino,
 as detailed below.
 * LEDs attached to each of the outputs of the shift register

 Created 22 May 2009
 Created 23 Mar 2010
 by Tom Igoe

 */

//Pin connected to latch pin (ST_CP) of 74HC595
const int latchPin = 8;
//Pin connected to clock pin (SH_CP) of 74HC595
const int clockPin = 12;
////Pin connected to Data in (DS) of 74HC595
const int dataPin = 11;

void setup() {
  //set pins to output because they are addressed in the main loop
  pinMode(latchPin, OUTPUT);
  pinMode(dataPin, OUTPUT);  
  pinMode(clockPin, OUTPUT);
  Serial.begin(9600);
  Serial.println("reset");
}

void loop() {
  if (Serial.available() > 0) {
    // ASCII '0' through '9' characters are
    // represented by the values 48 through 57.
    // so if the user types a number from 0 through 9 in ASCII, 
    // you can subtract 48 to get the actual value:
    int bitToSet = Serial.read() - 48;

  // write to the shift register with the correct bit set high:
    registerWrite(bitToSet, HIGH);
  }
}

// This method sends bits to the shift register:

void registerWrite(int whichPin, int whichState) {
// the bits you want to send
  byte bitsToSend = 0;

  // turn off the output so the pins don't light up
  // while you're shifting bits:
  digitalWrite(latchPin, LOW);

  // turn on the next highest bit in bitsToSend:
  bitWrite(bitsToSend, whichPin, whichState);

  // shift the bits out:
  shiftOut(dataPin, clockPin, MSBFIRST, bitsToSend);

    // turn on the output so the LEDs can light up:
  digitalWrite(latchPin, HIGH);

}
