# Fritzing sketch 555PWM (saved by Fritzing 0.9.3b)
circuit board: 2.26601cm x 4.63079cm
breadboards: 1

parts:
  R2 = Resistor [tolerance=±5% resistance=10k package=THT]
  D1 = Rectifier Diode [part_number=1N4001 package="300 mil [THT]"]
  D2 = Rectifier Diode [part_number=1N4001 package="300 mil [THT]"]
  D3 = Rectifier Diode [part_number=1N4001 package="300 mil [THT]"]
  TIP122 = npn-Powertransistor [package="TO220 [THT]"]
  555 = 555 Timer [package="DIP8 [THT]"]
  100µF = Electrolytic Capacitor [capacitance=10µF voltage=20V package="100 mil [THT, electrolytic]"]
  R3 = Resistor [tolerance=±5% resistance=1k package=THT]
  OUT = screw terminal, 2 pins
  C2 = Ceramic Capacitor [capacitance=0.1µF package="200 mil [THT, multilayer]"]
  C3 = Ceramic Capacitor [capacitance=0.1µF package="200 mil [THT, multilayer]"]
  5-16_Vin = screw terminal, 2 pins
  R1 = Rotary Potentiometer (Large) [maximum_resistance=100kΩ package=THT]

nets:
  12V: R2.Pin_0, D3.cathode, 555.Reset, 555.Vcc_Supply_Voltage, 100µF.+, OUT.pin1, 5-16_Vin.pin1
  N1: R2.Pin_1, 555.Discharge, R3.Pin_0
  N2: D1.cathode, R1.leg1
  N3: D1.anode, D2.cathode, 555.Trigger, 555.Threshold, C2.1
  N4: D2.anode, R1.leg2
  N5: D3.anode, TIP122.collector, OUT.pin2
  N6: TIP122.base, R3.Pin_1
  GND: TIP122.emitter, 555.Ground, 100µF.-, C2.0, C3.0, 5-16_Vin.pin2
  N7: 555.Output, R1.wiper
  N8: 555.Control_Voltage, C3.1

notes:
  -  +
  IN
  OUT
  PWM  Module with 555 Timer, This is an example of a PWM circuit using a 555 timing chip., 3
  Input voltage: 5-16V DC.
  Max current draw: 5A DC.
  R1 is an audio-taper pot.
